// Logisim project 04_contador_assincrono_crescente.circ as structural Verilog: 1 circuit, main circuit main
module main (
  input  in_1,
  input  CLR_prime,
  output Q3,
  output Q2,
  output Q1
);

  wire clock_1_out, FF1_qn, FF2_qn, not_1_out;

  Clock clock_1 (.out(clock_1_out));
  not not_1 (not_1_out, CLR_prime);
  J_K_Flip_Flop FF1 (.J(in_1), .clk(clock_1_out), .K(in_1), .Q(Q1), .Qn(FF1_qn), .reset(not_1_out));  // open: preset
  J_K_Flip_Flop FF2 (.J(in_1), .clk(FF1_qn), .K(in_1), .Q(Q2), .Qn(FF2_qn), .reset(not_1_out));  // open: preset
  J_K_Flip_Flop FF3 (.J(in_1), .clk(FF2_qn), .K(in_1), .Q(Q3), .reset(not_1_out));  // open: Qn, preset

  // Notes on the sheet:
  //   04 - Contador Assincrono crescente
endmodule
