// Logisim project 05_contador_assincrono_decrescente.circ as structural Verilog: 1 circuit, main circuit main
module main (
  input  clr,
  output out_2,
  output out_3,
  output out_4
);

  wire clock_1_out;

  Clock clock_1 (.out(clock_1_out));
  J_K_Flip_Flop FF1 (.J(1'b1), .clk(clock_1_out), .K(1'b1), .Q(out_2), .reset(clr));  // open: Qn, preset
  J_K_Flip_Flop FF2 (.J(1'b1), .clk(out_2), .K(1'b1), .Q(out_3), .reset(clr));  // open: Qn, preset
  J_K_Flip_Flop FF3 (.J(1'b1), .clk(out_3), .K(1'b1), .Q(out_4), .reset(clr));  // open: Qn, preset

  // Notes on the sheet:
  //   05 - Contador Assincrono decrescente
endmodule
