// Logisim project 06_contador_sincrono_crescente.circ as structural Verilog: 1 circuit, main circuit main
module main (
  input  in_1,
  input  CLR_prime,
  output Q3,
  output Q2,
  output Q1
);

  wire and_1_out, clock_1_out, not_1_out;

  Clock clock_1 (.out(clock_1_out));
  not not_1 (not_1_out, CLR_prime);
  J_K_Flip_Flop FF1 (.J(in_1), .clk(clock_1_out), .K(in_1), .Q(Q1), .reset(not_1_out));  // open: Qn, preset
  J_K_Flip_Flop FF2 (.J(Q1), .clk(clock_1_out), .K(Q1), .Q(Q2), .reset(not_1_out));  // open: Qn, preset
  and and_1 (and_1_out, Q1, Q2);
  J_K_Flip_Flop FF3 (.J(and_1_out), .clk(clock_1_out), .K(and_1_out), .Q(Q3), .reset(not_1_out));  // open: Qn, preset

  // Notes on the sheet:
  //   06 - Contador "Sincrono" Crescente
endmodule
