// Logisim project q02.circ as structural Verilog: 1 circuit, main circuit main
module main (
  input  in_1,
  input  clr,
  output out_3,
  output out_4,
  output out_5,
  output out_6,
  output out_7,
  output out_8
);

  wire clock_1_out;

  Clock clock_1 (.out(clock_1_out));
  J_K_Flip_Flop ff0 (.J(in_1), .clk(clock_1_out), .K(in_1), .Qn(out_8), .reset(clr));  // open: Q, preset
  J_K_Flip_Flop ff1 (.J(in_1), .clk(out_8), .K(in_1), .Qn(out_7), .reset(clr));  // open: Q, preset
  J_K_Flip_Flop ff2 (.J(in_1), .clk(out_7), .K(in_1), .Qn(out_6), .reset(clr));  // open: Q, preset
  J_K_Flip_Flop ff3 (.J(in_1), .clk(out_6), .K(in_1), .Qn(out_5), .reset(clr));  // open: Q, preset
  J_K_Flip_Flop ff4 (.J(in_1), .clk(out_5), .K(in_1), .Qn(out_4), .reset(clr));  // open: Q, preset
  J_K_Flip_Flop ff4_2 (.J(in_1), .clk(out_4), .K(in_1), .Qn(out_3), .reset(clr));  // open: Q, preset
endmodule
