// Logisim project q03.circ as structural Verilog: 1 circuit, main circuit main
module main (
  input  in_1,
  input  clr,
  output out_3,
  output out_4,
  output out_5,
  output out_6
);

  wire and_1_out, clock_1_out, ff0_qn, ff1_qn, ff2_qn, or_1_out;

  Clock clock_1 (.out(clock_1_out));
  J_K_Flip_Flop ff0 (.J(in_1), .clk(clock_1_out), .K(in_1), .Q(out_6), .Qn(ff0_qn), .reset(or_1_out));  // open: preset
  J_K_Flip_Flop ff1 (.J(in_1), .clk(ff0_qn), .K(in_1), .Q(out_5), .Qn(ff1_qn), .reset(or_1_out));  // open: preset
  or or_1 (or_1_out, and_1_out, clr);
  and and_1 (and_1_out, out_5, out_3);
  J_K_Flip_Flop ff2 (.J(in_1), .clk(ff1_qn), .K(in_1), .Q(out_4), .Qn(ff2_qn), .reset(or_1_out));  // open: preset
  J_K_Flip_Flop ff3 (.J(in_1), .clk(ff2_qn), .K(in_1), .Q(out_3), .reset(or_1_out));  // open: Qn, preset
endmodule
