// Logisim project Guia_12.circ as structural Verilog: 10 circuits, main circuit main
module main (
  input  Address,
  input  R_W,
  input  Address_2,
  input  CLR,
  input  CLR_2,
  input  R_W_2,
  input  IN,
  input  IN_2,
  input  Address_3,
  input  CLR_3,
  input  R_W_3,
  input  [3:0] IN_3,
  input  [1:0] sel,
  output OUT,
  output OUT_2,
  output [3:0] OUT_3
);

  wire and_1_out, and_3_out, and_4_out, and_5_out, and_6_out, clock_2_out, clock_3_out, clock_out, d_ff_1_q,
       j_k_ff_1_q, j_k_ff_2_q, multiplexer_1_out, not_1_out, not_2_out;

  Clock clock (.out(clock_out));
  Clock clock_2 (.out(clock_2_out));
  and and_1 (and_1_out, Address, R_W, clock_out);
  Multiplexer #(.select(2), .enable("false")) multiplexer_1 (
    .in0(IN_3[0]), .in1(IN_3[1]), .in2(IN_3[2]), .in3(IN_3[3]), .out(multiplexer_1_out), .sel(sel));
  and and_2 (OUT, Address, d_ff_1_q);
  D_Flip_Flop d_ff_1 (.clk(and_1_out), .D(IN), .Q(d_ff_1_q), .reset(CLR));  // open: Qn, preset
  not not_1 (not_1_out, and_3_out);
  and and_3 (and_3_out, Address_3, R_W_3, multiplexer_1_out);
  Clock clock_3 (.out(clock_3_out));
  J_K_Flip_Flop j_k_ff_1 (
    .J(and_3_out), .clk(clock_2_out), .K(not_1_out), .Q(j_k_ff_1_q), .reset(CLR_3));  // open: Qn, preset
  and and_4 (and_4_out, Address_2, R_W_2);
  and and_5 (and_5_out, Address_3, clock_2_out, j_k_ff_1_q);
  not not_2 (not_2_out, and_6_out);
  and and_6 (and_6_out, and_4_out, IN_2);
  Multiplexer #(.width(4), .enable("false")) multiplexer_2 (.in1(IN_3), .out(OUT_3), .sel(and_5_out));  // open: in0
  J_K_Flip_Flop j_k_ff_2 (
    .J(and_6_out), .clk(clock_3_out), .K(not_2_out), .Q(j_k_ff_2_q), .reset(CLR_2));  // open: Qn, preset
  and and_7 (OUT_2, Address_2, j_k_ff_2_q);
endmodule

// RAM 1x4
module Guia_1201 (
  input  [3:0] INPUT,
  input  R_W,
  input  ADDR,
  input  CLR,
  output [3:0] out_5
);

  wire AJ0_out, AJ1_out, AJ2_out, AJ3_out, AK0_out, AK1_out, AK2_out, AK3_out, and_1_out, CLK_out, not_1_out,
       not_2_out, not_3_out, not_4_out;

  and and_1 (and_1_out, R_W, ADDR);
  not not_1 (not_1_out, INPUT[2]);
  not not_2 (not_2_out, INPUT[3]);
  Clock CLK (.out(CLK_out));
  and AJ0 (AJ0_out, INPUT[0], and_1_out);
  not not_3 (not_3_out, INPUT[0]);
  and AK0 (AK0_out, not_3_out, and_1_out);
  and AJ1 (AJ1_out, INPUT[1], and_1_out);
  not not_4 (not_4_out, INPUT[1]);
  and AK1 (AK1_out, not_4_out, and_1_out);
  and AJ2 (AJ2_out, INPUT[2], and_1_out);
  and AK2 (AK2_out, not_1_out, and_1_out);
  and AJ3 (AJ3_out, INPUT[3], and_1_out);
  and AK3 (AK3_out, not_2_out, and_1_out);
  J_K_Flip_Flop FF0 (.J(AJ0_out), .clk(CLK_out), .K(AK0_out), .Q(out_5[0]), .reset(CLR));  // open: Qn, preset
  J_K_Flip_Flop FF1 (.J(AJ1_out), .clk(CLK_out), .K(AK1_out), .Q(out_5[1]), .reset(CLR));  // open: Qn, preset
  J_K_Flip_Flop FF2 (.J(AJ2_out), .clk(CLK_out), .K(AK2_out), .Q(out_5[2]), .reset(CLR));  // open: Qn, preset
  J_K_Flip_Flop FF3 (.J(AJ3_out), .clk(CLK_out), .K(AK3_out), .Q(out_5[3]), .reset(CLR));  // open: Qn, preset
endmodule

// 1x8
module Guia_1202___RAM_1x8 (
  input  R_W,
  input  ADDR,
  input  CLK,
  input  CLR,
  input  [7:0] IN,
  output [7:0] OUT
);

  Guia_1201___RAM_1x4 guia_1201_ram_1x4_1 (
    .INPUT(IN[3:0]), .CLOCK(CLK), .CLR(CLR), .R_W(R_W), .ADDR(ADDR), .out_6(OUT[3:0]));
  Guia_1201___RAM_1x4 guia_1201_ram_1x4_2 (
    .INPUT(IN[7:4]), .CLOCK(CLK), .CLR(CLR), .R_W(R_W), .ADDR(ADDR), .out_6(OUT[7:4]));

  // Notes on the sheet:
  //   RAM 1x8
endmodule

// RAM 1x4
module Guia_1201___RAM_1x4 (
  input  R_W,
  input  ADDR,
  input  [3:0] INPUT,
  input  CLOCK,
  input  CLR,
  output [3:0] out_6
);

  wire AJ0_out, AJ1_out, AJ2_out, AJ3_out, AK0_out, AK1_out, AK2_out, AK3_out, and_1_out, not_1_out,
       not_2_out, not_3_out, not_4_out;

  and and_1 (and_1_out, R_W, ADDR);
  not not_1 (not_1_out, INPUT[0]);
  not not_2 (not_2_out, INPUT[1]);
  and AJ2 (AJ2_out, INPUT[2], and_1_out);
  not not_3 (not_3_out, INPUT[2]);
  and AK2 (AK2_out, not_3_out, and_1_out);
  and AJ3 (AJ3_out, INPUT[3], and_1_out);
  not not_4 (not_4_out, INPUT[3]);
  and AK3 (AK3_out, not_4_out, and_1_out);
  and AJ0 (AJ0_out, INPUT[0], and_1_out);
  and AK0 (AK0_out, not_1_out, and_1_out);
  and AJ1 (AJ1_out, INPUT[1], and_1_out);
  and AK1 (AK1_out, not_2_out, and_1_out);
  J_K_Flip_Flop FF0 (.J(AJ0_out), .clk(CLOCK), .K(AK0_out), .Q(out_6[0]), .reset(CLR));  // open: Qn, preset
  J_K_Flip_Flop FF2 (.J(AJ2_out), .clk(CLOCK), .K(AK2_out), .Q(out_6[2]), .reset(CLR));  // open: Qn, preset
  J_K_Flip_Flop FF1 (.J(AJ1_out), .clk(CLOCK), .K(AK1_out), .Q(out_6[1]), .reset(CLR));  // open: Qn, preset
  J_K_Flip_Flop FF3 (.J(AJ3_out), .clk(CLOCK), .K(AK3_out), .Q(out_6[3]), .reset(CLR));  // open: Qn, preset

  // Notes on the sheet:
  //   RAM 1x4
endmodule

// 2x8
module Guia_1203___RAM_2x8 (
  input  R_W,
  input  ADDR,
  input  CLK,
  input  CLR,
  input  [7:0] IN,
  output [7:0] out_6
);

  wire not_1_out;
  wire [3:0] guia_1201_ram_1x4_1_out_6, guia_1201_ram_1x4_2_out_6, guia_1201_ram_1x4_3_out_6,
       guia_1201_ram_1x4_4_out_6;

  Guia_1201___RAM_1x4 guia_1201_ram_1x4_1 (
    .INPUT(IN[3:0]), .CLOCK(CLK), .CLR(CLR), .R_W(R_W), .ADDR(ADDR), .out_6(guia_1201_ram_1x4_1_out_6));
  Guia_1201___RAM_1x4 guia_1201_ram_1x4_2 (
    .INPUT(IN[7:4]), .CLOCK(CLK), .CLR(CLR), .R_W(R_W), .ADDR(ADDR), .out_6(guia_1201_ram_1x4_2_out_6));
  Guia_1201___RAM_1x4 guia_1201_ram_1x4_3 (
    .INPUT(IN[3:0]), .CLOCK(CLK), .CLR(CLR), .R_W(R_W), .ADDR(not_1_out), .out_6(guia_1201_ram_1x4_3_out_6));
  Guia_1201___RAM_1x4 guia_1201_ram_1x4_4 (
    .INPUT(IN[7:4]), .CLOCK(CLK), .CLR(CLR), .R_W(R_W), .ADDR(not_1_out), .out_6(guia_1201_ram_1x4_4_out_6));
  not not_1 (not_1_out, ADDR);
  Multiplexer #(.width(8), .enable("false")) multiplexer_1 (
    .in0({guia_1201_ram_1x4_2_out_6, guia_1201_ram_1x4_1_out_6}),
    .in1({guia_1201_ram_1x4_4_out_6, guia_1201_ram_1x4_3_out_6}), .out(out_6), .sel(not_1_out));

  // Notes on the sheet:
  //   RAM 2x8
endmodule

// 4x8
module Guia_1204___RAM_4x8 (
  input  R_W,
  input  ADDR,
  input  CLK,
  input  CLR,
  input  [7:0] in_5,
  output [7:0] out_6
);

  wire not_1_out;
  wire [7:0] guia_1203_ram_2x8_1_out_6, guia_1203_ram_2x8_2_out_6;

  Guia_1203___RAM_2x8 guia_1203_ram_2x8_1 (
    .CLK(CLK), .CLR(CLR), .IN(in_5), .R_W(R_W), .ADDR(ADDR), .out_6(guia_1203_ram_2x8_1_out_6));
  not not_1 (not_1_out, ADDR);
  Guia_1203___RAM_2x8 guia_1203_ram_2x8_2 (
    .CLK(CLK), .CLR(CLR), .IN(in_5), .R_W(R_W), .ADDR(not_1_out), .out_6(guia_1203_ram_2x8_2_out_6));
  Multiplexer #(.width(8), .enable("false")) multiplexer_1 (
    .in0(guia_1203_ram_2x8_1_out_6), .in1(guia_1203_ram_2x8_2_out_6), .out(out_6), .sel(not_1_out));

  // Notes on the sheet:
  //   RAM 4x8
endmodule

module Guia_1205___RAM_8x8 (
  input  ADDR,
  input  R_W,
  input  [7:0] RAM_8x8,
  input  CLR,
  output [7:0] out_5
);

  wire clock_1_out, not_1_out;
  wire [7:0] guia_1204_ram_4x8_1_out_6, guia_1204_ram_4x8_2_out_6;

  not not_1 (not_1_out, ADDR);
  Clock clock_1 (.out(clock_1_out));
  Guia_1204___RAM_4x8 guia_1204_ram_4x8_1 (
    .R_W(R_W), .ADDR(ADDR), .CLK(clock_1_out), .CLR(CLR), .in_5(RAM_8x8), .out_6(guia_1204_ram_4x8_1_out_6));
  Multiplexer #(.width(8), .enable("false")) multiplexer_1 (
    .in0(guia_1204_ram_4x8_1_out_6), .in1(guia_1204_ram_4x8_2_out_6), .out(out_5), .sel(not_1_out));
  Guia_1204___RAM_4x8 guia_1204_ram_4x8_2 (
    .R_W(R_W), .ADDR(not_1_out), .CLK(clock_1_out), .CLR(CLR), .in_5(RAM_8x8),
    .out_6(guia_1204_ram_4x8_2_out_6));
endmodule

module Guia_1206___RAM_4x16 (
  input  ADDR,
  input  R_W,
  input  [15:0] in_3,
  input  CLR,
  output [15:0] out_5
);

  wire clock_1_out;

  Clock clock_1 (.out(clock_1_out));
  Guia_1204___RAM_4x8 guia_1204_ram_4x8_1 (
    .R_W(R_W), .ADDR(ADDR), .CLK(clock_1_out), .CLR(CLR), .in_5(in_3[7:0]), .out_6(out_5[7:0]));
  Guia_1204___RAM_4x8 guia_1204_ram_4x8_2 (
    .R_W(R_W), .ADDR(ADDR), .CLK(clock_1_out), .CLR(CLR), .in_5(in_3[15:8]), .out_6(out_5[15:8]));

  // Notes on the sheet:
  //   RAM 4x16
endmodule

module Guia_1207___RAM_8x16 (
  input  CLR,
  input  CLK,
  input  R_W,
  input  [15:0] IN,
  input  [2:0] ADDR,
  output [15:0] OUT
);

  wire demultiplexer_1_out0, demultiplexer_1_out1, demultiplexer_1_out2, demultiplexer_1_out3,
       demultiplexer_1_out4, demultiplexer_1_out5, demultiplexer_1_out6, demultiplexer_1_out7;
  wire [15:0] ram_1x16_1_out, ram_1x16_2_out, ram_1x16_3_out, ram_1x16_4_out, ram_1x16_5_out, ram_1x16_6_out,
       ram_1x16_7_out, ram_1x16_8_out;

  Demultiplexer #(.select(3), .enable("false")) demultiplexer_1 (
    .out0(demultiplexer_1_out0), .out1(demultiplexer_1_out1), .out2(demultiplexer_1_out2),
    .out3(demultiplexer_1_out3), .out4(demultiplexer_1_out4), .out5(demultiplexer_1_out5),
    .out6(demultiplexer_1_out6), .out7(demultiplexer_1_out7), .in(1'b1), .sel(ADDR));
  RAM___1x16 ram_1x16_1 (.OUT(ram_1x16_1_out), .IN(IN), .CLR(CLR), .CLK(CLK), .R_W(R_W), .ADDR(demultiplexer_1_out0));
  RAM___1x16 ram_1x16_2 (.OUT(ram_1x16_2_out), .IN(IN), .CLR(CLR), .CLK(CLK), .R_W(R_W), .ADDR(demultiplexer_1_out1));
  RAM___1x16 ram_1x16_3 (.OUT(ram_1x16_3_out), .IN(IN), .CLR(CLR), .CLK(CLK), .R_W(R_W), .ADDR(demultiplexer_1_out2));
  RAM___1x16 ram_1x16_4 (.OUT(ram_1x16_4_out), .IN(IN), .CLR(CLR), .CLK(CLK), .R_W(R_W), .ADDR(demultiplexer_1_out3));
  RAM___1x16 ram_1x16_5 (.OUT(ram_1x16_5_out), .IN(IN), .CLR(CLR), .CLK(CLK), .R_W(R_W), .ADDR(demultiplexer_1_out4));
  RAM___1x16 ram_1x16_6 (.OUT(ram_1x16_6_out), .IN(IN), .CLR(CLR), .CLK(CLK), .R_W(R_W), .ADDR(demultiplexer_1_out5));
  RAM___1x16 ram_1x16_7 (.OUT(ram_1x16_7_out), .IN(IN), .CLR(CLR), .CLK(CLK), .R_W(R_W), .ADDR(demultiplexer_1_out6));
  RAM___1x16 ram_1x16_8 (.OUT(ram_1x16_8_out), .IN(IN), .CLR(CLR), .CLK(CLK), .R_W(R_W), .ADDR(demultiplexer_1_out7));
  Multiplexer #(.select(3), .width(16), .enable("false")) multiplexer_1 (
    .in0(ram_1x16_1_out), .in1(ram_1x16_2_out), .in2(ram_1x16_3_out), .in3(ram_1x16_4_out),
    .in4(ram_1x16_5_out), .in5(ram_1x16_6_out), .in6(ram_1x16_7_out), .in7(ram_1x16_8_out), .out(OUT),
    .sel(ADDR));

  // Notes on the sheet:
  //   RAM 8x16
endmodule

// 1x16
module RAM___1x16 (
  input  CLR,
  input  CLK,
  input  R_W,
  input  ADDR,
  input  [15:0] IN,
  output [15:0] OUT
);

  Guia_1202___RAM_1x8 guia_1202_ram_1x8_1 (.CLK(CLK), .CLR(CLR), .IN(IN[7:0]), .R_W(R_W), .ADDR(ADDR), .OUT(OUT[7:0]));
  Guia_1202___RAM_1x8 guia_1202_ram_1x8_2 (
    .CLK(CLK), .CLR(CLR), .IN(IN[15:8]), .R_W(R_W), .ADDR(ADDR), .OUT(OUT[15:8]));

  // Notes on the sheet:
  //   RAM 1x16
endmodule
