// Logisim project Guia_11.circ as structural Verilog: 6 circuits, main circuit Ex. 1 - Mealy_1101
module Ex__1___Mealy_1101 (
  input  x,
  input  Reset,
  output y
);

  wire Clock_out, FF0_q, FF1_q, FF1_qn, FF2_q, FF3_q, undriven;

  Clock Clock (.out(Clock_out));
  D_Flip_Flop FF0 (.clk(Clock_out), .D(x), .Q(FF0_q), .reset(Reset));  // open: Qn, preset
  D_Flip_Flop FF1 (.clk(Clock_out), .D(FF0_q), .Q(FF1_q), .Qn(FF1_qn), .reset(Reset));  // open: preset
  D_Flip_Flop FF2 (.clk(Clock_out), .D(FF1_q), .Q(FF2_q), .reset(Reset));  // open: Qn, preset
  D_Flip_Flop FF3 (.clk(Clock_out), .D(FF2_q), .Q(FF3_q), .preset(undriven), .reset(Reset));  // open: Qn
  and and_1 (y, FF3_q, FF2_q, FF1_qn, FF0_q);
endmodule

module Ex__2___Moore_1101 (
  input  x,
  input  Reset,
  output y
);

  wire Clock_out, FF0_q, FF1_q, FF1_qn, FF2_q, FF3_q, undriven;

  Clock Clock (.out(Clock_out));
  D_Flip_Flop FF0 (.clk(Clock_out), .D(x), .Q(FF0_q), .reset(Reset));  // open: Qn, preset
  D_Flip_Flop FF1 (.clk(Clock_out), .D(FF0_q), .Q(FF1_q), .Qn(FF1_qn), .reset(Reset));  // open: preset
  D_Flip_Flop FF2 (.clk(Clock_out), .D(FF1_q), .Q(FF2_q), .reset(Reset));  // open: Qn, preset
  D_Flip_Flop FF3 (.clk(Clock_out), .D(FF2_q), .Q(FF3_q), .preset(undriven), .reset(Reset));  // open: Qn
  and and_1 (y, FF3_q, FF2_q, FF1_qn, FF0_q);
endmodule

module Ex__3___Guia_1100 (
  input  x,
  input  Reset,
  input  x_2,
  input  Reset_2,
  output y,
  output y_2
);

  wire and_1_out, and_2_out, Clock_2_out, Clock_out, FF0_2_q, FF0_q, FF0_qn, FF1_2_q, FF1_q, FF1_qn, FF2_q,
       FF3_q, or_1_out, undriven;

  Clock Clock (.out(Clock_out));
  Clock Clock_2 (.out(Clock_2_out));
  D_Flip_Flop FF0 (.clk(Clock_out), .D(x_2), .Q(FF0_q), .Qn(FF0_qn), .reset(Reset_2));  // open: preset
  D_Flip_Flop FF0_2 (.clk(Clock_2_out), .D(x), .Q(FF0_2_q), .reset(Reset));  // open: Qn, preset
  or or_1 (or_1_out, FF1_2_q, x_2);
  D_Flip_Flop FF1 (.clk(Clock_2_out), .D(FF0_2_q), .Q(FF1_q), .Qn(FF1_qn), .reset(Reset));  // open: preset
  and and_1 (and_1_out, FF0_q, or_1_out);
  D_Flip_Flop FF2 (.clk(Clock_2_out), .D(FF1_q), .Q(FF2_q), .reset(Reset));  // open: Qn, preset
  D_Flip_Flop FF1_2 (.clk(Clock_out), .D(and_1_out), .Q(FF1_2_q), .reset(Reset_2));  // open: Qn, preset
  D_Flip_Flop FF3 (.clk(Clock_2_out), .D(FF2_q), .Q(FF3_q), .preset(undriven), .reset(Reset));  // open: Qn
  and and_2 (and_2_out, FF1_2_q, FF0_qn, x_2);
  and and_3 (y, FF3_q, FF2_q, FF1_qn, FF0_2_q);
  D_Flip_Flop FF2_2 (.clk(Clock_out), .D(and_2_out), .Q(y_2), .reset(Reset_2));  // open: Qn, preset

  // Notes on the sheet:
  //   Guia_1100: Moore - 1101
  //   Guia_1100: Mealy - 1101
endmodule

module Ex__4___Guia_1101 (
  input  x,
  input  Reset,
  output y
);

  wire and_1_out, Clock_out, FF0_q, FF0_qn, FF1_q, FF2_q, FF2_qn, FF3_q, FF_IDENT_q, FF_IDENT_qn, or_1_out,
       undriven;

  Clock Clock (.out(Clock_out));
  D_Flip_Flop FF0 (.clk(Clock_out), .D(x), .Q(FF0_q), .Qn(FF0_qn), .reset(Reset));  // open: preset
  D_Flip_Flop FF1 (.clk(Clock_out), .D(FF0_q), .Q(FF1_q), .reset(Reset));  // open: Qn, preset
  D_Flip_Flop FF2 (.clk(Clock_out), .D(FF1_q), .Q(FF2_q), .Qn(FF2_qn), .reset(Reset));  // open: preset
  D_Flip_Flop FF3 (.clk(Clock_out), .D(FF2_q), .Q(FF3_q), .preset(undriven), .reset(Reset));  // open: Qn
  or or_1 (or_1_out, FF_IDENT_q, and_1_out);
  and and_1 (and_1_out, FF3_q, FF2_qn, FF1_q, FF0_qn);
  D_Flip_Flop FF_IDENT (
    .clk(Clock_out), .D(or_1_out), .Q(FF_IDENT_q), .Qn(FF_IDENT_qn), .reset(Reset));  // open: preset
  and and_2 (y, FF_IDENT_qn, and_1_out);

  // Notes on the sheet:
  //   Moore 1010 - 1ª sequencia
endmodule

module Ex__5___Guia_1102 (
  input  x,
  input  clk,
  input  clear,
  output s
);

  wire ff0_q, ff0_qn, ff1_q, ff2_q, or_1_out;

  D_Flip_Flop ff0 (.clk(x), .D(clk), .Q(ff0_q), .Qn(ff0_qn), .reset(or_1_out));  // open: preset
  D_Flip_Flop ff1 (.clk(ff0_q), .Q(ff1_q), .Qn(ff0_qn), .reset(or_1_out));  // open: D, preset
  or or_1 (or_1_out, clear, s);
  D_Flip_Flop ff2 (.clk(ff1_q), .Q(ff2_q), .reset(or_1_out));  // open: D, Qn, preset
  and and_1 (s, x, ff2_q, ff0_qn, ff0_qn);

  // Notes on the sheet:
  //   Mealy 1001 - 1ª sequencia
endmodule

module Ex__6___Guia_1103 (
  input  x,
  input  Reset,
  output y
);

  wire Clock_out, FF0_q, FF1_q, FF2_q, FF2_qn, FF3_q, FF3_qn, undriven;

  Clock Clock (.out(Clock_out));
  D_Flip_Flop FF0 (.clk(Clock_out), .D(x), .Q(FF0_q), .reset(Reset));  // open: Qn, preset
  D_Flip_Flop FF1 (.clk(Clock_out), .D(FF0_q), .Q(FF1_q), .reset(Reset));  // open: Qn, preset
  D_Flip_Flop FF2 (.clk(Clock_out), .D(FF1_q), .Q(FF2_q), .Qn(FF2_qn), .reset(Reset));  // open: preset
  D_Flip_Flop FF3 (.clk(Clock_out), .D(FF2_q), .Q(FF3_q), .Qn(FF3_qn), .preset(undriven), .reset(Reset));
  and and_1 (y, FF3_q, FF2_qn, FF1_q, FF0_q);

  // Notes on the sheet:
  //   Moore 1011 - com interseção
endmodule
