// Logisim project Guia_10.circ as structural Verilog: 2 circuits, main circuit Guia_1006
module Guia_1006 (
  output out_1
);

  wire clock_1_out, d_ff_1_q, d_ff_2_q, d_ff_2_qn, d_ff_3_q, d_ff_3_qn, d_ff_4_q, programmablegenerator_1_p1,
       programmablegenerator_2_p1;

  Clock clock_1 (.out(clock_1_out));
  // ProgrammableGenerator #(.nState(1)) programmablegenerator_1: pin names not known; wires that end beside it: programmablegenerator_1_p1
  // ProgrammableGenerator #(.nState(1)) programmablegenerator_2: pin names not known; wires that end beside it: programmablegenerator_2_p1
  D_Flip_Flop d_ff_1 (
    .clk(clock_1_out), .D(programmablegenerator_1_p1), .Q(d_ff_1_q), .reset(programmablegenerator_2_p1));  // open: Qn, preset
  D_Flip_Flop d_ff_2 (
    .clk(clock_1_out), .D(d_ff_1_q), .Q(d_ff_2_q), .Qn(d_ff_2_qn), .reset(programmablegenerator_2_p1));  // open: preset
  and and_1 (out_1, d_ff_4_q, d_ff_3_qn, d_ff_2_qn, d_ff_1_q);
  D_Flip_Flop d_ff_3 (
    .clk(clock_1_out), .D(d_ff_2_q), .Q(d_ff_3_q), .Qn(d_ff_3_qn), .reset(programmablegenerator_2_p1));  // open: preset
  D_Flip_Flop d_ff_4 (
    .clk(clock_1_out), .D(d_ff_3_q), .Q(d_ff_4_q), .reset(programmablegenerator_2_p1));  // open: Qn, preset
endmodule

module Guia_1007 (
  output out_1
);

  wire clock_1_out, d_ff_1_q, d_ff_1_qn, d_ff_2_q, d_ff_3_q, d_ff_3_qn, d_ff_4_q, programmablegenerator_1_p1,
       programmablegenerator_2_p1;

  Clock clock_1 (.out(clock_1_out));
  // ProgrammableGenerator #(.nState(1)) programmablegenerator_1: pin names not known; wires that end beside it: programmablegenerator_1_p1
  // ProgrammableGenerator #(.nState(1)) programmablegenerator_2: pin names not known; wires that end beside it: programmablegenerator_2_p1
  D_Flip_Flop d_ff_1 (
    .clk(clock_1_out), .D(programmablegenerator_1_p1), .Q(d_ff_1_q), .Qn(d_ff_1_qn),
    .reset(programmablegenerator_2_p1));  // open: preset
  D_Flip_Flop d_ff_2 (
    .clk(clock_1_out), .D(d_ff_1_q), .Q(d_ff_2_q), .reset(programmablegenerator_2_p1));  // open: Qn, preset
  and and_1 (out_1, d_ff_4_q, d_ff_3_qn, d_ff_2_q, d_ff_1_qn);
  D_Flip_Flop d_ff_3 (
    .clk(clock_1_out), .D(d_ff_2_q), .Q(d_ff_3_q), .Qn(d_ff_3_qn), .reset(programmablegenerator_2_p1));  // open: preset
  D_Flip_Flop d_ff_4 (
    .clk(clock_1_out), .D(d_ff_3_q), .Q(d_ff_4_q), .reset(programmablegenerator_2_p1));  // open: Qn, preset
endmodule
