// Logisim project guia0401.circ as structural Verilog: 1 circuit, main circuit main
module main (
  input  x,
  input  y,
  input  z,
  output out_4
);

  wire not_1_out, not_2_out, not_3_out, or_1_out;

  not not_1 (not_1_out, y);
  not not_2 (not_2_out, z);
  not not_3 (not_3_out, or_1_out);
  or or_1 (or_1_out, not_1_out, not_2_out);
  and and_1 (out_4, x, not_3_out);
endmodule
