// Logisim project guia0402.circ as structural Verilog: 1 circuit, main circuit main
module main (
  input  in_1,
  input  in_2,
  input  in_3,
  output out_4
);

  wire not_1_out, not_2_out, or_1_out;

  or or_1 (or_1_out, in_2, in_3);
  not not_1 (not_1_out, in_1);
  and and_1 (out_4, not_1_out, not_2_out);
  not not_2 (not_2_out, or_1_out);
endmodule
