// Logisim project guia0403.circ as structural Verilog: 1 circuit, main circuit main
module main (
  input  x,
  input  y,
  input  w,
  input  z,
  output out_5
);

  wire not_1_out, not_2_out, or_1_out;

  not not_1 (not_1_out, x);
  not not_2 (not_2_out, z);
  or or_1 (or_1_out, not_1_out, y, w);
  and and_1 (out_5, or_1_out, not_2_out);
endmodule
