// Logisim project guia0501.circ as structural Verilog: 1 circuit, main circuit main
module main (
  input  a,
  input  b,
  output out_3
);

  wire _1_out, _2_out, _3_out;

  nand _1 (_1_out, a, a);
  nand _2 (_2_out, b, b);
  nand _3 (_3_out, _1_out, _2_out);
  nand _4 (out_3, _3_out, _3_out);
endmodule
