// Logisim project guia0503.circ as structural Verilog: 1 circuit, main circuit main
module main (
  input  a,
  input  b,
  output out_3
);

  wire _1_out, _2_out;

  nand _1 (_1_out, b, b);
  nand _2 (_2_out, a, _1_out);
  nand _3 (out_3, _2_out, _2_out);
endmodule
