// Logisim project guia0504.circ as structural Verilog: 1 circuit, main circuit main
module main (
  input  a,
  input  b,
  output s
);

  wire _1_out, _2_out, _3_out;

  nor _1 (_1_out, a, a);
  nor _2 (_2_out, b, b);
  nor _3 (_3_out, _1_out, _2_out);
  nor _4 (s, _3_out, _3_out);
endmodule
