// Logisim project guia0505.circ as structural Verilog: 1 circuit, main circuit main
module main (
  input  a,
  input  b,
  output s
);

  wire q_out, w3_out, wa_out, wb_out;

  nand wb (wb_out, a, wa_out);
  nand wa (wa_out, a, b);
  nand w3 (w3_out, wa_out, b);
  nand q (q_out, wb_out, w3_out);
  nand nand_1 (s, q_out, q_out);
endmodule
