// Logisim project guia0506.circ as structural Verilog: 1 circuit, main circuit main
module main (
  input  a,
  input  b,
  output s
);

  wire _1_out, _2_out, _3_out, _4_out;

  nor _1 (_1_out, a, b);
  nor _2 (_2_out, a, _1_out);
  nor _3 (_3_out, _1_out, b);
  nor _4 (_4_out, _2_out, _3_out);
  nor _5 (s, _4_out, _4_out);
endmodule
