// Logisim project guia0507.circ as structural Verilog: 1 circuit, main circuit main
module main (
  input  in_1,
  input  b,
  output out_3
);

  wire _1_out, _2_out, _3_out, nand_1_out;

  nand nand_1 (nand_1_out, b, b);
  nand _1 (_1_out, in_1, nand_1_out);
  nand _2 (_2_out, in_1, _1_out);
  nand _4 (out_3, _2_out, _3_out);
  nand _3 (_3_out, _1_out, nand_1_out);
endmodule
