// Logisim project guia0508.circ as structural Verilog: 1 circuit, main circuit main
module main (
  input  a,
  input  b,
  output out_3
);

  wire _1_out, _2_out;

  nor _1 (_1_out, a, a);
  nor _2 (_2_out, _1_out, b);
  nor _3 (out_3, _2_out, _2_out);
endmodule
