// Logisim project q04c.circ as structural Verilog: 1 circuit, main circuit main
module main (
  input  a,
  input  b,
  input  c,
  output sb,
  output rb
);

  wire not_1_out, not_2_out;

  not not_1 (not_1_out, a);
  not not_2 (not_2_out, b);
  and and_1 (sb, not_1_out, not_2_out, c);
  and and_2 (rb, a, a, c);

  // Notes on the sheet:
  //   sb = a'b'c
  //   rb = abc
endmodule
