// Logisim project q04d.circ as structural Verilog: 1 circuit, main circuit main
module main (
  input  a,
  input  b,
  input  c,
  output ta
);

  wire and_1_out, and_2_out, not_1_out, not_2_out;

  not not_1 (not_1_out, a);
  not not_2 (not_2_out, b);
  and and_1 (and_1_out, not_1_out, not_2_out, c);
  and and_2 (and_2_out, b, a, c);
  or or_1 (ta, and_1_out, and_2_out);

  // Notes on the sheet:
  //   Tb = a'b'c + abc
endmodule
