// Logisim project q05a.circ as structural Verilog: 1 circuit, main circuit main
module main (
  input  i2,
  input  i3,
  input  i4,
  input  i5,
  input  i0,
  input  i1,
  input  load
);

  wire clock_1_out, d_ff_1_q, d_ff_2_q, d_ff_3_q, d_ff_4_q, d_ff_5_q, d_ff_6_q, multiplexer_1_out,
       multiplexer_2_out, multiplexer_3_out, multiplexer_4_out, multiplexer_5_out, multiplexer_6_out;

  Multiplexer #(.enable("false")) multiplexer_1 (.in0(i0), .in1(d_ff_6_q), .out(multiplexer_1_out), .sel(load));
  D_Flip_Flop d_ff_1 (.clk(clock_1_out), .D(multiplexer_1_out), .Q(d_ff_1_q));  // open: Qn, preset, reset
  Multiplexer #(.enable("false")) multiplexer_2 (.in0(i1), .in1(d_ff_1_q), .out(multiplexer_2_out), .sel(load));
  D_Flip_Flop d_ff_2 (.clk(clock_1_out), .D(multiplexer_2_out), .Q(d_ff_2_q));  // open: Qn, preset, reset
  Multiplexer #(.enable("false")) multiplexer_3 (.in0(i2), .in1(d_ff_2_q), .out(multiplexer_3_out), .sel(load));
  Clock clock_1 (.out(clock_1_out));
  D_Flip_Flop d_ff_3 (.clk(clock_1_out), .D(multiplexer_3_out), .Q(d_ff_3_q));  // open: Qn, preset, reset
  Multiplexer #(.enable("false")) multiplexer_4 (.in0(i3), .in1(d_ff_3_q), .out(multiplexer_4_out), .sel(load));
  D_Flip_Flop d_ff_4 (.clk(clock_1_out), .D(multiplexer_4_out), .Q(d_ff_4_q));  // open: Qn, preset, reset
  Multiplexer #(.enable("false")) multiplexer_5 (.in0(i4), .in1(d_ff_4_q), .out(multiplexer_5_out), .sel(load));
  Multiplexer #(.enable("false")) multiplexer_6 (.in0(i5), .in1(d_ff_5_q), .out(multiplexer_6_out), .sel(load));
  D_Flip_Flop d_ff_5 (.clk(clock_1_out), .D(multiplexer_5_out), .Q(d_ff_5_q));  // open: Qn, preset, reset
  D_Flip_Flop d_ff_6 (.clk(clock_1_out), .D(multiplexer_6_out), .Q(d_ff_6_q));  // open: Qn, preset, reset
endmodule
