// Logisim project q05b.circ as structural Verilog: 1 circuit, main circuit main
module main (
  input  i2,
  input  i3,
  input  i4,
  input  i5,
  input  i0,
  input  i1,
  input  load
);

  wire clock_1_out, ff0_q, ff1_q, ff2_q, ff3_q, ff4_q, ff5_q, multiplexer_1_out, multiplexer_2_out,
       multiplexer_3_out, multiplexer_4_out, multiplexer_5_out, multiplexer_6_out;

  Multiplexer #(.enable("false")) multiplexer_1 (.in0(i0), .in1(ff1_q), .out(multiplexer_1_out), .sel(load));
  D_Flip_Flop ff0 (.clk(clock_1_out), .D(multiplexer_1_out), .Q(ff0_q));  // open: Qn, preset, reset
  Multiplexer #(.enable("false")) multiplexer_2 (.in0(i1), .in1(ff2_q), .out(multiplexer_2_out), .sel(load));
  D_Flip_Flop ff1 (.clk(clock_1_out), .D(multiplexer_2_out), .Q(ff1_q));  // open: Qn, preset, reset
  Multiplexer #(.enable("false")) multiplexer_3 (.in0(i2), .in1(ff3_q), .out(multiplexer_3_out), .sel(load));
  Clock clock_1 (.out(clock_1_out));
  D_Flip_Flop ff2 (.clk(clock_1_out), .D(multiplexer_3_out), .Q(ff2_q));  // open: Qn, preset, reset
  Multiplexer #(.enable("false")) multiplexer_4 (.in0(i3), .in1(ff4_q), .out(multiplexer_4_out), .sel(load));
  D_Flip_Flop ff3 (.clk(clock_1_out), .D(multiplexer_4_out), .Q(ff3_q));  // open: Qn, preset, reset
  Multiplexer #(.enable("false")) multiplexer_5 (.in0(i4), .in1(ff5_q), .out(multiplexer_5_out), .sel(load));
  D_Flip_Flop ff4 (.clk(clock_1_out), .D(multiplexer_5_out), .Q(ff4_q));  // open: Qn, preset, reset
  Multiplexer #(.enable("false")) multiplexer_6 (.in0(i5), .in1(ff0_q), .out(multiplexer_6_out), .sel(load));
  D_Flip_Flop ff5 (.clk(clock_1_out), .D(multiplexer_6_out), .Q(ff5_q));  // open: Qn, preset, reset

  // Notes on the sheet:
  //   nao consegui implementar esse, não identifiquei qual o problema
endmodule
