// Logisim project questao03.circ as structural Verilog: 1 circuit, main circuit main
module main (
  input  c,
  input  a,
  input  b,
  output s
);

  wire an_out, bn_out, w1_out, w2_out, w3_out;

  nand an (an_out, a, a);
  nand bn (bn_out, b, b);
  nand w1 (w1_out, c, an_out);
  nand w2 (w2_out, an_out, b);
  nand nand_1 (s, w1_out, w2_out, w3_out);
  nand w3 (w3_out, c, bn_out);
endmodule
