// Logisim project questao2a.circ as structural Verilog: 1 circuit, main circuit main
module main (
  input  a,
  input  b,
  input  c,
  output out_4
);

  wire not_1_out, w1_out;

  not not_1 (not_1_out, c);
  or w1 (w1_out, b, not_1_out);
  and and_1 (out_4, a, w1_out);
endmodule
