// Logisim project questao4.circ as structural Verilog: 1 circuit, main circuit main
module main (
  input  a,
  input  b,
  input  c,
  output out_4
);

  wire and_1_out, and_2_out, and_3_out, not_1_out, not_2_out;

  not not_1 (not_1_out, a);
  and and_1 (and_1_out, not_1_out, not_2_out);
  not not_2 (not_2_out, c);
  and and_2 (and_2_out, b, not_2_out);
  and and_3 (and_3_out, c, not_1_out);
  or or_1 (out_4, and_1_out, and_2_out, and_3_out);
endmodule
